// Logisim project 8051.circ as structural Verilog: 5 circuits, main circuit main
module main (
  input  Reset
);

  wire adder_1_cout, alu_v2_1_auxiliarycarryflag, alu_v2_1_carryflag, alu_v2_1_overflowflag,
       alu_v2_1_signflag, alu_v2_1_zeroflag, CarryFlag, CLK_out, clock_1_out, clock_2_out,
       controlunit_1_incrementpc, controlunit_1_indirectaddressingmode, controlunit_1_registerload,
       controlunit_1_registerstore, decoder_1_out0, decoder_1_out1, decoder_1_out2, decoder_1_out3,
       decoder_1_out4, decoder_1_out5, decoder_1_out6, decoder_1_out7, decoder_1_out8, decoder_1_out9,
       decoder_1_out10, decoder_1_out11, decoder_1_out12, decoder_1_out13, decoder_1_out14, decoder_1_out15,
       decoder_1_out16, decoder_1_out19, or_1_out, or_2_out, psw_1_auxiliarycarryflagout,
       psw_1_overflowflagout, SignFlag, ZeroFlag;
  wire [3:0] controlunit_1_alu_opcode;
  wire [4:0] controlled_buffer_1_out, controlunit_1_registeraddress, multiplexer_2_out, multiplexer_3_out,
       SourceRegister_q;
  wire [7:0] adder_1_out, ALU_Buffer1_q, ALU_Buffer2_q, ALU_Output_q, ALU_OutputAux_q, alu_v2_1_accumulator,
       alu_v2_1_alu_outputaux, bit_extender_1_out, controlled_buffer_2_out, ControlUnitDataBuffer_q,
       InstructionRegister_q, multiplexer_1_out, OpcodeLowerNibble_q, ProgramCounter_q, R0_q, R1_q, R2_q,
       R3_q, R4_q, R5_q, R6_q, R7_q, RegisterA_q, RegisterB_q, undriven, undriven_2, undriven_3, undriven_4,
       xCode_data;
  wire [7:5] SourceRegister_q_2;

  Multiplexer #(.width(8)) multiplexer_1 (
    .in0(controlled_buffer_2_out), .in1(adder_1_out), .out(multiplexer_1_out), .sel(controlunit_1_incrementpc));
  assign bit_extender_1_out = {{7{1'b0}}, controlunit_1_incrementpc};  // Bit_Extender bit_extender_1
  Register ProgramCounter (
    .D(multiplexer_1_out), .en(or_1_out), .clk(clock_1_out), .Q(ProgramCounter_q), .clr(or_2_out));
  or or_1 (or_1_out, controlunit_1_incrementpc, decoder_1_out19);
  Clock clock_1 (.out(clock_1_out));
  Adder adder_1 (.a(ProgramCounter_q), .b(bit_extender_1_out), .out(adder_1_out), .cout(adder_1_cout));  // open: cin
  or or_2 (or_2_out, adder_1_cout, Reset);
  Comparator #(.mode("unsigned")) comparator_1 (.a(ProgramCounter_q), .b({8{1'b1}}), .eq(Reset));  // open: gt, lt
  Clock clock_2 (.out(clock_2_out));
  ROM xCode (.addr(ProgramCounter_q), .data(xCode_data));
  Decoder #(.select(5)) decoder_1 (
    .out0(decoder_1_out0), .out1(decoder_1_out1), .out2(decoder_1_out2), .out3(decoder_1_out3),
    .out4(decoder_1_out4), .out5(decoder_1_out5), .out6(decoder_1_out6), .out7(decoder_1_out7),
    .out8(decoder_1_out8), .out9(decoder_1_out9), .out10(decoder_1_out10), .out11(decoder_1_out11),
    .out12(decoder_1_out12), .out13(decoder_1_out13), .out14(decoder_1_out14), .out15(decoder_1_out15),
    .out16(decoder_1_out16), .out19(decoder_1_out19), .sel(multiplexer_2_out),
    .en(controlunit_1_registerstore));  // open: out17, out18, out20, out21, out22, out23, out24, out25, out26, out27, out28, out29, out30, out31
  // NoConnect on decoder_1_out4
  // NoConnect on decoder_1_out5
  Multiplexer #(.width(5)) multiplexer_2 (
    .in0(controlunit_1_registeraddress), .in1(SourceRegister_q), .out(multiplexer_2_out),
    .sel(controlunit_1_indirectaddressingmode));
  ControlUnit controlunit_1 (
    .InstructionLine(xCode_data), .CLK(clock_2_out), .CarryFlag(CarryFlag), .ZeroFlag(ZeroFlag),
    .RegisterAddress(controlunit_1_registeraddress), .ALU_Opcode(controlunit_1_alu_opcode),
    .RegisterLoad(controlunit_1_registerload), .RegisterStore(controlunit_1_registerstore),
    .IncrementPC(controlunit_1_incrementpc), .IndirectAddressingMode(controlunit_1_indirectaddressingmode));
  Register ALU_Buffer1 (
    .D(controlled_buffer_2_out), .en(decoder_1_out0), .clk(CLK_out), .Q(ALU_Buffer1_q), .clr(Reset));
  Register ALU_Buffer2 (
    .D(controlled_buffer_2_out), .en(decoder_1_out1), .clk(CLK_out), .Q(ALU_Buffer2_q), .clr(Reset));
  Register RegisterA (.D(controlled_buffer_2_out), .en(decoder_1_out2), .clk(CLK_out), .Q(RegisterA_q), .clr(Reset));
  Register RegisterB (.D(controlled_buffer_2_out), .en(decoder_1_out3), .clk(CLK_out), .Q(RegisterB_q), .clr(Reset));
  Register ALU_Output (.D(alu_v2_1_accumulator), .en(1'b1), .clk(CLK_out), .Q(ALU_Output_q), .clr(Reset));
  Clock CLK (.out(CLK_out));
  Multiplexer #(.width(5)) multiplexer_3 (
    .in0(controlunit_1_registeraddress), .in1(SourceRegister_q), .out(multiplexer_3_out),
    .sel(controlunit_1_indirectaddressingmode));
  Register R0 (.D(controlled_buffer_2_out), .en(decoder_1_out8), .clk(CLK_out), .Q(R0_q), .clr(Reset));
  Register R1 (.D(controlled_buffer_2_out), .en(decoder_1_out9), .clk(CLK_out), .Q(R1_q), .clr(Reset));
  Register R2 (.D(controlled_buffer_2_out), .en(decoder_1_out10), .clk(CLK_out), .Q(R2_q), .clr(Reset));
  Register R3 (.D(controlled_buffer_2_out), .en(decoder_1_out11), .clk(CLK_out), .Q(R3_q), .clr(Reset));
  Register R4 (.D(controlled_buffer_2_out), .en(decoder_1_out12), .clk(CLK_out), .Q(R4_q), .clr(Reset));
  Register R5 (.D(controlled_buffer_2_out), .en(decoder_1_out13), .clk(CLK_out), .Q(R5_q), .clr(Reset));
  Register R6 (.D(controlled_buffer_2_out), .en(decoder_1_out14), .clk(CLK_out), .Q(R6_q), .clr(Reset));
  Register R7 (.D(controlled_buffer_2_out), .en(decoder_1_out15), .clk(CLK_out), .Q(R7_q), .clr(Reset));
  assign controlled_buffer_1_out = controlunit_1_registerload ? multiplexer_3_out : 5'bz;  // Controlled_Buffer controlled_buffer_1
  Register SourceRegister (
    .D(controlled_buffer_2_out), .en(decoder_1_out16), .clk(CLK_out),
    .Q({SourceRegister_q_2, SourceRegister_q}), .clr(Reset));
  Register OpcodeLowerNibble (
    .D({4'b0000, xCode_data[3:0]}), .en(1'b1), .clk(CLK_out), .Q(OpcodeLowerNibble_q), .clr(Reset));
  Register InstructionRegister (.D(xCode_data), .en(1'b1), .clk(CLK_out), .Q(InstructionRegister_q), .clr(Reset));
  ALU_v2 alu_v2_1 (
    .OverflowIn(psw_1_overflowflagout), .AuxiliaryCarryIn(psw_1_auxiliarycarryflagout), .CarryIn(CarryFlag),
    .Buffer1(ALU_Buffer1_q), .Buffer2(ALU_Buffer2_q), .Opcode(controlunit_1_alu_opcode),
    .Accumulator(alu_v2_1_accumulator), .ALU_OutputAux(alu_v2_1_alu_outputaux),
    .CarryFlag(alu_v2_1_carryflag), .ZeroFlag(alu_v2_1_zeroflag), .SignFlag(alu_v2_1_signflag),
    .AuxiliaryCarryFlag(alu_v2_1_auxiliarycarryflag), .OverflowFlag(alu_v2_1_overflowflag));
  Register ControlUnitDataBuffer (
    .D(controlled_buffer_2_out), .en(controlunit_1_registerload), .clk(CLK_out), .Q(ControlUnitDataBuffer_q),
    .clr(Reset));
  assign controlled_buffer_2_out = controlunit_1_registerstore ? ControlUnitDataBuffer_q : 8'bz;  // Controlled_Buffer controlled_buffer_2
  // NoConnect on undriven_3
  // NoConnect on undriven_4
  Multiplexer #(.select(5), .width(8)) multiplexer_4 (
    .in0(undriven_3), .in1(undriven_4), .in2(RegisterA_q), .in3(RegisterB_q), .in4(ALU_Output_q),
    .in5(ALU_OutputAux_q), .in6(undriven_2), .in7(undriven), .in8(R0_q), .in9(R1_q), .in10(R2_q),
    .in11(R3_q), .in12(R4_q), .in13(R5_q), .in14(R6_q), .in15(R7_q),
    .in16({SourceRegister_q_2, SourceRegister_q}), .in17(OpcodeLowerNibble_q), .in18(InstructionRegister_q),
    .in19(ProgramCounter_q), .out(controlled_buffer_2_out), .sel(controlled_buffer_1_out));  // open: in20, in21, in22, in23, in24, in25, in26, in27, in28, in29, in30, in31
  Register ALU_OutputAux (.D(alu_v2_1_alu_outputaux), .en(1'b1), .clk(CLK_out), .Q(ALU_OutputAux_q));  // open: clr
  PSW psw_1 (
    .CarryFlagIn(alu_v2_1_carryflag), .ZeroFlagIn(alu_v2_1_zeroflag), .CLK(CLK_out),
    .OverflowFlagIn(alu_v2_1_overflowflag), .SignFlagIn(alu_v2_1_signflag),
    .AuxiliaryCarryIn(alu_v2_1_auxiliarycarryflag), .ZeroFlagOut(ZeroFlag), .CarryFlagOut(CarryFlag),
    .OverflowFlagOut(psw_1_overflowflagout), .SignFlagOut(SignFlag),
    .AuxiliaryCarryFlagOut(psw_1_auxiliarycarryflagout));

  // Notes on the sheet:
  //   registerAddressForInput
  //   contents of xCode (hex, n*v repeats v):
  //   2a 99 99 5*0 99
  //   RegisterSelectBus
  //   indirect addressing: @R0, @R1
  //   Data Bus
  //   zeroing upper nibble
  //   registerAddressForOutput
endmodule

module ALU_v2 (
  input  OverflowIn,
  input  AuxiliaryCarryIn,
  input  CarryIn,
  input  [7:0] Buffer1,
  input  [7:0] Buffer2,
  input  [3:0] Opcode,
  output [7:0] Accumulator,
  output [7:0] ALU_OutputAux,
  output CarryFlag,
  output ZeroFlag,
  output SignFlag,
  output AuxiliaryCarryFlag,
  output OverflowFlag
);

  wire adder_4_cout, adder_5_cout, adder_6_cout, adder_7_cout, adder_8_cout, adder_10_cout, comparator_1_lt,
       comparator_2_lt, comparator_3_lt, comparator_5_eq, comparator_5_gt, nor_1_out, or_1_out, xor_1_out,
       xor_2_out, xor_4_out;
  wire [6:0] adder_9_out, negator_2_out;
  wire [7:0] adder_1_out, adder_2_out, adder_3_out, adder_4_out, adder_5_out, adder_6_out, and_1_out,
       and_2_out, and_3_out, bit_extender_3_out, bit_extender_4_out, divider_1_out, divider_1_rem,
       multiplier_1_out, negator_1_out, or_2_out, shifter_1_out, shifter_2_out, undriven, xor_3_out;
  wire [15:0] bit_extender_1_out, bit_extender_2_out;
  wire [15:8] multiplier_1_out_2;

  Adder adder_1 (.a({8{1'b0}}), .b(Buffer2), .out(adder_1_out), .cin(CarryIn));  // open: cout
  Negator negator_1 (.in(adder_1_out), .out(negator_1_out));
  assign bit_extender_1_out = {{8{Buffer2[7]}}, Buffer2};  // Bit_Extender bit_extender_1
  assign bit_extender_2_out = {{8{Buffer1[7]}}, Buffer1};  // Bit_Extender bit_extender_2
  Comparator #(.mode("unsigned")) comparator_1 (.a(Buffer1), .b(Buffer2), .lt(comparator_1_lt));  // open: gt, eq
  Adder adder_2 (.a(8'h1), .b(Buffer1), .out(adder_2_out));  // open: cin, cout
  Adder adder_3 (.a({8{1'b1}}), .b(Buffer1), .out(adder_3_out));  // open: cin, cout
  Adder adder_4 (.a(Buffer1), .b(Buffer2), .out(adder_4_out), .cout(adder_4_cout));  // open: cin
  Adder adder_5 (.a(Buffer1), .b(Buffer2), .out(adder_5_out), .cin(CarryIn), .cout(adder_5_cout));
  Adder adder_6 (.a(Buffer1), .b(negator_1_out), .out(adder_6_out), .cout(adder_6_cout));  // open: cin
  Multiplier #(.width(16)) multiplier_1 (
    .a(bit_extender_1_out), .b(bit_extender_2_out), .out({multiplier_1_out_2, multiplier_1_out}));  // open: cin, cout
  Adder #(.width(4)) adder_7 (.a(Buffer1[3:0]), .b(Buffer2[3:0]), .cout(adder_7_cout));  // open: out, cin
  Adder #(.width(4)) adder_8 (.a(Buffer1[3:0]), .b(Buffer2[3:0]), .cin(CarryIn), .cout(adder_8_cout));  // open: out
  xor xor_1 (xor_1_out, CarryIn, adder_4_cout);
  Divider divider_1 (.a(Buffer1), .b(Buffer2), .out(divider_1_out), .rem(divider_1_rem));  // open: upper
  Comparator #(.mode("unsigned"), .width(4)) comparator_2 (
    .a(Buffer1[3:0]), .b(Buffer2[3:0]), .lt(comparator_2_lt));  // open: gt, eq
  xor xor_2 (xor_2_out, CarryIn, adder_5_cout);
  or or_1 (or_1_out, multiplier_1_out_2[8], multiplier_1_out_2[9], multiplier_1_out_2[10], multiplier_1_out_2[11], multiplier_1_out_2[12], multiplier_1_out_2[13], multiplier_1_out_2[14], multiplier_1_out_2[15]);
  nor nor_1 (nor_1_out, Buffer2[0], Buffer2[1], Buffer2[2], Buffer2[3], Buffer2[4], Buffer2[5], Buffer2[6], Buffer2[7]);
  Shifter #(.shift("rr")) shifter_1 (.in(Buffer1), .\dist (3'b001), .out(shifter_1_out));
  Shifter #(.shift("rl")) shifter_2 (.in(Buffer1), .\dist (3'b001), .out(shifter_2_out));
  // NoConnect on undriven
  assign or_2_out = Buffer1 | Buffer2;  // OR_Gate or_2, 8 bits wide
  assign and_1_out = Buffer1 & Buffer2;  // AND_Gate and_1, 8 bits wide
  assign xor_3_out = Buffer1 ^ Buffer2;  // XOR_Gate xor_3, 8 bits wide
  Comparator comparator_3 (.a(Buffer1), .b(Buffer2), .lt(comparator_3_lt));  // open: gt, eq
  Comparator #(.mode("unsigned")) comparator_4 (.a(Buffer1), .b(Buffer2), .eq(ZeroFlag), .lt(SignFlag));  // open: gt
  Adder #(.width(7)) adder_9 (.a({7{1'b0}}), .b(Buffer2[6:0]), .out(adder_9_out), .cin(CarryIn));  // open: cout
  Multiplexer #(.select(4), .width(8)) multiplexer_1 (
    .in0(adder_2_out), .in1(adder_3_out), .in2(adder_4_out), .in3(adder_5_out), .in4(adder_6_out),
    .in5(multiplier_1_out), .in6(divider_1_out), .in7(or_2_out), .in8(and_1_out), .in9(xor_3_out),
    .in10(undriven), .in11(shifter_1_out), .in12(shifter_1_out), .in13(shifter_2_out), .in14(shifter_2_out),
    .in15(Buffer1), .out(Accumulator), .sel(Opcode));
  Adder #(.width(7)) adder_10 (.a(Buffer1[6:0]), .b(negator_2_out), .cout(adder_10_cout));  // open: out, cin
  Negator #(.width(7)) negator_2 (.in(adder_9_out), .out(negator_2_out));
  Comparator #(.mode("unsigned"), .width(4)) comparator_5 (
    .a(Opcode), .b(4'b0101), .gt(comparator_5_gt), .eq(comparator_5_eq));  // open: lt
  xor xor_4 (xor_4_out, adder_6_cout, adder_10_cout);
  assign bit_extender_3_out = {{7{comparator_5_eq}}, comparator_5_eq};  // Bit_Extender bit_extender_3
  assign bit_extender_4_out = {{7{comparator_5_gt}}, comparator_5_gt};  // Bit_Extender bit_extender_4
  Multiplexer #(.select(4)) multiplexer_2 (
    .in0(CarryIn), .in1(CarryIn), .in2(adder_4_cout), .in3(adder_5_cout), .in4(comparator_1_lt), .in5(1'b0),
    .in6(1'b0), .in7(CarryIn), .in8(CarryIn), .in9(CarryIn), .in10(comparator_3_lt), .in12(Buffer1[0]),
    .in14(Buffer1[7]), .out(CarryFlag), .sel(Opcode));  // open: in11, in13, in15
  Multiplexer #(.select(4)) multiplexer_3 (
    .in0(CarryIn), .in1(CarryIn), .in2(adder_7_cout), .in3(adder_8_cout), .in4(comparator_2_lt),
    .in5(AuxiliaryCarryIn), .in6(AuxiliaryCarryIn), .in7(AuxiliaryCarryIn), .in8(AuxiliaryCarryIn),
    .in9(AuxiliaryCarryIn), .in10(AuxiliaryCarryIn), .out(AuxiliaryCarryFlag), .sel(Opcode));  // open: in11, in12, in13, in14, in15
  Multiplexer #(.select(4)) multiplexer_4 (
    .in0(CarryIn), .in1(CarryIn), .in2(xor_1_out), .in3(xor_2_out), .in4(xor_4_out), .in5(or_1_out),
    .in6(nor_1_out), .in7(OverflowIn), .in8(OverflowIn), .in9(OverflowIn), .in10(OverflowIn),
    .out(OverflowFlag), .sel(Opcode));  // open: in11, in12, in13, in14, in15
  assign and_2_out = bit_extender_3_out & multiplier_1_out_2;  // AND_Gate and_2, 8 bits wide
  assign and_3_out = bit_extender_4_out & divider_1_rem;  // AND_Gate and_3, 8 bits wide
  assign ALU_OutputAux = and_2_out | and_3_out;  // OR_Gate or_3, 8 bits wide

  // Notes on the sheet:
  //   ACC ->
  //   2. operand ->
  //   cin
  //   A
  //   B
endmodule

module ControlUnit (
  input  [7:0] InstructionLine,
  input  CLK,
  input  CarryFlag,
  input  ZeroFlag,
  output [4:0] RegisterAddress,
  output [3:0] ALU_Opcode,
  output RegisterLoad,
  output RegisterStore,
  output IncrementPC,
  output IndirectAddressingMode
);

  wire comparator_1_eq, multiplexer_1_out, or_1_out, undriven, undriven_2;
  wire [3:0] ALU_OpcodeRegister_q, and_1_out, and_2_out, bit_extender_1_out, OpcodeToALU_Opcode_out,
       or_2_out, pla_1_out, sequencegenerator_1_value;
  wire [20:0] multiplexer_3_out;
  wire [23:0] add_imm_1_coded_output, div_mul_1_coded_output, djnz_1_coded_output, inc_dec_1_coded_output,
       jc_1_coded_output, jnc_1_coded_output, jnz_1_coded_output, mov_acc_to_reg_1_coded_output,
       mov_reg_to_acc_1_coded_output, rotate_1_coded_output, xchg_1_coded_output;

  PLA #(.in_width(8), .out_width(4), .\table ("00000011 1011 # rr\n00010011 1100 # rrc\n00100011 1101 # rl\n00110011 1110 # rlc\n0000x1xx 0000 # inc\n0001x1xx 0001 # dec\n0010xxxx 0010 # add\n0011x1xx 0011 # addc\n0100xx10 0111 # orl\n0101xxxx 1000 # anl\n1001x1xx 0100 # subb\n11011xxx 1010 # compare (djnz)\n0110xxxx 1001 # xrl")) OpcodeToALU_Opcode (
    .in(InstructionLine), .out(OpcodeToALU_Opcode_out));
  ROTATE rotate_1 (.ADDRESS(sequencegenerator_1_value), .CODED_OUTPUT(rotate_1_coded_output));
  XCHG xchg_1 (.ADDRESS(sequencegenerator_1_value), .CODED_OUTPUT(xchg_1_coded_output));
  JC jc_1 (.ADDRESS(sequencegenerator_1_value), .CODED_OUTPUT(jc_1_coded_output));
  JNC jnc_1 (.ADDRESS(sequencegenerator_1_value), .CODED_OUTPUT(jnc_1_coded_output));
  DJNZ djnz_1 (.ADDRESS(sequencegenerator_1_value), .CODED_OUTPUT(djnz_1_coded_output));
  DIV_MUL div_mul_1 (.ADDRESS(sequencegenerator_1_value), .CODED_OUTPUT(div_mul_1_coded_output));
  ADD_imm add_imm_1 (.ADDRESS(sequencegenerator_1_value), .CODED_OUTPUT(add_imm_1_coded_output));
  JNZ jnz_1 (.ADDRESS(sequencegenerator_1_value), .CODED_OUTPUT(jnz_1_coded_output));
  MOV_reg_to_acc mov_reg_to_acc_1 (.ADDRESS(sequencegenerator_1_value), .CODED_OUTPUT(mov_reg_to_acc_1_coded_output));
  MOV_acc_to_reg mov_acc_to_reg_1 (.ADDRESS(sequencegenerator_1_value), .CODED_OUTPUT(mov_acc_to_reg_1_coded_output));
  INC_DEC inc_dec_1 (.ADDRESS(sequencegenerator_1_value), .CODED_OUTPUT(inc_dec_1_coded_output));
  Register #(.width(4)) ALU_OpcodeRegister (
    .D(OpcodeToALU_Opcode_out), .en(1'b1), .clk(CLK), .Q(ALU_OpcodeRegister_q));  // open: clr
  // NoConnect on undriven
  // NoConnect on undriven_2
  Multiplexer #(.select(2)) multiplexer_1 (
    .in0(undriven), .in1(CarryFlag), .in2(ZeroFlag), .in3(undriven_2), .out(multiplexer_1_out),
    .sel({multiplexer_3_out[1], multiplexer_3_out[2]}));
  assign bit_extender_1_out = {{3{multiplexer_1_out}}, multiplexer_1_out};  // Bit_Extender bit_extender_1
  or or_1 (or_1_out, multiplexer_3_out[2], multiplexer_3_out[1]);
  Comparator #(.mode("unsigned"), .width(4)) comparator_1 (
    .a(multiplexer_3_out[20:17]), .b(4'b0000), .eq(comparator_1_eq));  // open: gt, lt
  PLA #(.in_width(8), .out_width(4), .\table ("00xx0011 0000 # rr, rrc, rl, rlc\n1100xxxx 0001 # xch\n01000000 0010 # jc\n01010000 0011 # jnc\n11011xxx 0100 # djnz\n10x00100 0101 # div, mul\n00100100 0110 # add (immediate)\n01110000 0111 # jnz\n11101xxx 1000 # mov (to ACC to GPR)\n11111xxx 1001 # mov (from ACC to GPR)\n00x01xxx 1010 # inc, dec\n0110xxxx 1010 # xrl\n0101xxxx 0000 # anl")) pla_1 (
    .in(InstructionLine), .out(pla_1_out));
  assign and_1_out = multiplexer_3_out[10:7] & bit_extender_1_out;  // AND_Gate and_1, 4 bits wide
  assign and_2_out = ~bit_extender_1_out & multiplexer_3_out[6:3];  // AND_Gate and_2, 4 bits wide
  Multiplexer #(.width(4)) multiplexer_2 (
    .in0(multiplexer_3_out[20:17]), .in1(ALU_OpcodeRegister_q), .out(ALU_Opcode), .sel(comparator_1_eq));
  Multiplexer #(.select(4), .width(24)) multiplexer_3 (
    .in0(rotate_1_coded_output), .in1(xchg_1_coded_output), .in2(jc_1_coded_output),
    .in3(jnc_1_coded_output), .in4(djnz_1_coded_output), .in5(div_mul_1_coded_output),
    .in6(add_imm_1_coded_output), .in7(jnz_1_coded_output), .in8(mov_reg_to_acc_1_coded_output),
    .in9(mov_acc_to_reg_1_coded_output), .in10(inc_dec_1_coded_output),
    .out({IncrementPC, RegisterStore, RegisterLoad, multiplexer_3_out[20:17], RegisterAddress, IndirectAddressingMode, multiplexer_3_out[10:0]}),
    .sel(pla_1_out));  // open: in11, in12, in13, in14, in15
  assign or_2_out = and_1_out | and_2_out;  // OR_Gate or_2, 4 bits wide
  SequenceGenerator sequencegenerator_1 (
    .LoadData(or_1_out), .Reset(multiplexer_3_out[0]), .CLK(CLK), .Data(or_2_out),
    .Value(sequencegenerator_1_value));  // open: Completed

  // Notes on the sheet:
  //   opcode to instruction groups
endmodule

module SequenceGenerator (
  input  LoadData,
  input  Reset,
  input  CLK,
  input  [3:0] Data,
  output Completed,
  output [3:0] Value
);

  wire not_1_out;

  Counter #(.max('hf), .ongoal("stay"), .width(4)) counter_1 (
    .clr(Reset), .load(LoadData), .up(1'b1), .count(not_1_out), .clk(CLK), .D(Data), .carry(Completed),
    .Q(Value));
  not not_1 (not_1_out, Reset);
endmodule

module PSW (
  input  CarryFlagIn,
  input  ZeroFlagIn,
  input  CLK,
  input  OverflowFlagIn,
  input  SignFlagIn,
  input  AuxiliaryCarryIn,
  output ZeroFlagOut,
  output CarryFlagOut,
  output OverflowFlagOut,
  output SignFlagOut,
  output AuxiliaryCarryFlagOut
);

  D_Flip_Flop ZeroFlag (.D(ZeroFlagIn), .clk(AuxiliaryCarryIn), .Q(ZeroFlagOut));  // open: Qn, preset, reset
  D_Flip_Flop CarryFlag (.D(AuxiliaryCarryIn), .clk(AuxiliaryCarryIn), .Q(CarryFlagOut));  // open: Qn, preset, reset
  D_Flip_Flop OverflowFlag (
    .D(AuxiliaryCarryIn), .clk(AuxiliaryCarryIn), .Q(OverflowFlagOut));  // open: Qn, preset, reset
  D_Flip_Flop SignFlag (.D(AuxiliaryCarryIn), .clk(AuxiliaryCarryIn), .Q(SignFlagOut));  // open: Qn, preset, reset
  D_Flip_Flop AuxiliaryCarryFlag (
    .D(AuxiliaryCarryIn), .clk(AuxiliaryCarryIn), .Q(AuxiliaryCarryFlagOut));  // open: Qn, preset, reset

  assign CarryFlagIn = AuxiliaryCarryIn;
  assign CLK = AuxiliaryCarryIn;
  assign OverflowFlagIn = AuxiliaryCarryIn;
  assign SignFlagIn = AuxiliaryCarryIn;
endmodule
