// Logisim project ROMy.circ as structural Verilog: 13 circuits, main circuit main
module main (
  input  [3:0] ADDRESS,
  output [23:0] CODED_OUTPUT
);

  ROM #(.addrWidth(4), .dataWidth(24)) rom_1 (.addr(ADDRESS), .data(CODED_OUTPUT));
endmodule

module JC (
  input  [3:0] ADDRESS,
  output [23:0] CODED_OUTPUT
);

  ROM #(.addrWidth(4), .dataWidth(24)) rom_1 (.addr(ADDRESS), .data(CODED_OUTPUT));

  // Notes on the sheet:
  //   contents of rom_1 (hex, n*v repeats v):
  //   0 1bc 0 800000 212000 413000 1 800001
endmodule

module JNC (
  input  [3:0] ADDRESS,
  output [23:0] CODED_OUTPUT
);

  ROM #(.addrWidth(4), .dataWidth(24)) rom_1 (.addr(ADDRESS), .data(CODED_OUTPUT));

  // Notes on the sheet:
  //   contents of rom_1 (hex, n*v repeats v):
  //   0 39c 0 800000 212000 413000 1 800001
endmodule

module ROTATE (
  input  [3:0] ADDRESS,
  output [23:0] CODED_OUTPUT
);

  ROM #(.addrWidth(4), .dataWidth(24)) rom_1 (.addr(ADDRESS), .data(CODED_OUTPUT));

  // Notes on the sheet:
  //   contents of rom_1 (hex, n*v repeats v):
  //   0 202000 400000 204000 402000 800001
endmodule

module JNZ (
  input  [3:0] ADDRESS,
  output [23:0] CODED_OUTPUT
);

  ROM #(.addrWidth(4), .dataWidth(24)) rom_1 (.addr(ADDRESS), .data(CODED_OUTPUT));

  // Notes on the sheet:
  //   contents of rom_1 (hex, n*v repeats v):
  //   202000 0 400000 23a 800000 212000 413000 1 800001
endmodule

module DJNZ (
  input  [3:0] ADDRESS,
  output [23:0] CODED_OUTPUT
);

  ROM #(.addrWidth(4), .dataWidth(24)) rom_1 (.addr(ADDRESS), .data(CODED_OUTPUT));

  // Notes on the sheet:
  //   contents of rom_1 (hex, n*v repeats v):
  //   800000 212000 20000 400000 204000 0 400000 462 800000 212000 413000 1 800001
endmodule

module DIV_MUL (
  input  [3:0] ADDRESS,
  output [23:0] CODED_OUTPUT
);

  ROM #(.addrWidth(4), .dataWidth(24)) rom_1 (.addr(ADDRESS), .data(CODED_OUTPUT));

  // Notes on the sheet:
  //   contents of rom_1 (hex, n*v repeats v):
  //   0 202000 400000 203000 401000 204000 402000 205000 403000 800001
endmodule

module ADD_imm (
  input  [3:0] ADDRESS,
  output [23:0] CODED_OUTPUT
);

  ROM #(.addrWidth(4), .dataWidth(24)) rom_1 (.addr(ADDRESS), .data(CODED_OUTPUT));

  // Notes on the sheet:
  //   contents of rom_1 (hex, n*v repeats v):
  //   0 800000 212000 401000 202000 400000 40000 204000 402000 800001
endmodule

module XCHG (
  input  [3:0] ADDRESS,
  output [23:0] CODED_OUTPUT
);

  ROM #(.addrWidth(4), .dataWidth(24)) rom_1 (.addr(ADDRESS), .data(CODED_OUTPUT));

  // Notes on the sheet:
  //   contents of rom_1 (hex, n*v repeats v):
  //   0 211000 410000 202000 403000 210800 402000 203000 410800 800001
endmodule

module MOV_reg_to_acc (
  input  [3:0] ADDRESS,
  output [23:0] CODED_OUTPUT
);

  ROM #(.addrWidth(4), .dataWidth(24)) rom_1 (.addr(ADDRESS), .data(CODED_OUTPUT));

  // Notes on the sheet:
  //   contents of rom_1 (hex, n*v repeats v):
  //   0 211000 410000 210800 402000 800001
endmodule

module MOV_acc_to_reg (
  input  [3:0] ADDRESS,
  output [23:0] CODED_OUTPUT
);

  ROM #(.addrWidth(4), .dataWidth(24)) rom_1 (.addr(ADDRESS), .data(CODED_OUTPUT));

  // Notes on the sheet:
  //   contents of rom_1 (hex, n*v repeats v):
  //   0 211000 410000 202000 410800 800001
endmodule

module INC_DEC (
  input  [3:0] ADDRESS,
  output [23:0] CODED_OUTPUT
);

  ROM #(.addrWidth(4), .dataWidth(24)) rom_1 (.addr(ADDRESS), .data(CODED_OUTPUT));

  // Notes on the sheet:
  //   contents of rom_1 (hex, n*v repeats v):
  //   0 211000 410000 210800 400000 0 204000 402000 800001
endmodule

module ADD_reg (
  input  [3:0] ADDRESS,
  output [23:0] CODED_OUTPUT
);

  ROM #(.addrWidth(4), .dataWidth(24)) rom_1 (.addr(ADDRESS), .data(CODED_OUTPUT));

  // Notes on the sheet:
  //   contents of rom_1 (hex, n*v repeats v):
  //   0 211000 410000 210800 401000 202000 400000 40000 204000 402000 800001
endmodule
